// Logisim project MIPS32.circ as structural Verilog
module Fetch (
);

  wire clock_1_out;
  wire [1:0] incrementer_1_p3;
  wire [29:0] incrementer_1_p1, incrementer_1_p2;

  Clock clock_1 (.out(clock_1_out));
  // Incrementer #(.width(30)) incrementer_1: pin names not known; wires that end beside it: incrementer_1_p1, incrementer_1_p2, {incrementer_1_p1, incrementer_1_p3}
  Register #(.width(32)) register_1 (
    .D({incrementer_1_p2, incrementer_1_p3}), .en(clock_1_out), .clk(clock_1_out),
    .Q({incrementer_1_p1, incrementer_1_p3}));  // open: clr
  // MIPSProgramROM mipsprogramrom_1: pin names not known

  // Notes on the sheet:
  //   contents of mipsprogramrom_1 (hex, n*v repeats v):
  //   ADDIU $t2, $zero, 1 ADDU $v0, $t1, $t2 ADDU $t1, $zero, $t2 ADDU $t2, $zero, $v0 ADDU $v0, $t1, $t2
  //   ADDU $t1, $zero, $t2 ADDU $t2, $zero, $v0 ADDU $v0, $t1, $t2 ADDU $t1, $zero, $t2 ADDU $t2, $zero,
  //   $v0
endmodule

module Decode (
  input  [31:0] Word,
  output [31:0] A,
  output [31:0] B,
  output [31:0] Immediate,
  output [31:0] Ctrl
);

  wire [4:0] multiplexer_1_out, multiplexer_2_out;
  wire [31:0] bit_extender_1_out, bit_extender_2_out;

  Multiplexer #(.width(5), .enable("false")) multiplexer_1 (
    .in0(Word[15:11]), .in1(Word[20:16]), .out(multiplexer_1_out), .sel(Word[29]));
  assign bit_extender_1_out = {{16{Word[15]}}, Word[15:0]};  // Bit_Extender bit_extender_1
  assign bit_extender_2_out = {{16{1'b0}}, Word[15:0]};  // Bit_Extender bit_extender_2
  Multiplexer #(.width(5), .enable("false")) multiplexer_2 (
    .in0(multiplexer_1_out), .in1(Word[20:16]), .out(multiplexer_2_out), .sel(Word[31]));
  // RegisterFile registerfile_1: pin names not known; wires that end beside it: multiplexer_2_out, Word[25:21], Word[20:16], A, B
  Multiplexer #(.width(32), .enable("false")) multiplexer_3 (
    .in0(bit_extender_1_out), .in1(bit_extender_2_out), .out(Immediate), .sel(Word[28]));

  assign Ctrl = Word;
endmodule

module Execute (
  input  [31:0] A,
  input  [31:0] B,
  input  [31:0] Immediate,
  input  [31:0] Ctrl
);

  wire mips_alu_1_p2, mips_alu_1_p5, mips_alu_1_p6, mips_alu_1_p7;
  wire [5:0] multiplexer_2_out;
  wire [31:0] multiplexer_1_out;

  Multiplexer #(.width(32), .enable("false")) multiplexer_1 (
    .in0(B), .in1(Immediate), .out(multiplexer_1_out), .sel(Ctrl[29]));
  Multiplexer #(.width(6), .enable("false")) multiplexer_2 (
    .in0(Ctrl[5:0]), .in1(Ctrl[31:26]), .out(multiplexer_2_out), .sel(Ctrl[29]));
  // Mips_ALU mips_alu_1: pin names not known; wires that end beside it: multiplexer_1_out, mips_alu_1_p2, mips_alu_1_p2, Ctrl[10:6], mips_alu_1_p5, mips_alu_1_p6, mips_alu_1_p7
  Comparator #(.width(32)) comparator_1 (.gt(mips_alu_1_p5), .eq(mips_alu_1_p6), .lt(mips_alu_1_p7));  // open: a, b
endmodule
